# Fritzing sketch ESP8266_Blynk_LED (saved by Fritzing 0.9.3b)
breadboards: 1

parts:
  U1 = 2-Channel 5v Relay Shield [package=relay-2ch5v10a]
  U2 = NodeMCU V3.0
  S1 = Pushbutton [package="[THT]"]
  R1 = Resistor [tolerance=±5% resistance=1k package=THT]

nets:
  VCC: U1.VCC, U2.3V3
  N1: U1.GND, U2.GND#6, U2.GND#13, U2.GND#16, U2.GND#33, S1.Pin_3, S1.Pin_4
  N2: U1.IN1, U2.D1
  N3: U1.IN2, U2.D0
  N4: U2.D2, R1.Pin_1
  N5: S1.Pin_1, S1.Pin_2, R1.Pin_0

custom parts:
  2-Channel 5v Relay Shield: 2 Channel 5v Relay Shield w. 2x SPD-06VDC-SD-C
  NodeMCU V3.0: ESP8266 based NodeMCU
